// Logisim project decoder_lab.circ as structural Verilog
module number_encoder (
  input  [7:0] number,
  output [2:0] binary
);

  wire not_1_out, not_2_out, not_3_out, not_4_out, not_5_out, not_6_out, not_7_out, not_8_out, not_9_out,
       not_10_out, not_11_out, not_12_out;

  not not_1 (not_1_out, number[3]);
  not not_2 (not_2_out, number[2]);
  not not_3 (not_3_out, number[1]);
  not not_4 (not_4_out, number[0]);
  not not_5 (not_5_out, number[5]);
  not not_6 (not_6_out, number[4]);
  not not_7 (not_7_out, number[1]);
  not not_8 (not_8_out, number[0]);
  not not_9 (not_9_out, number[6]);
  not not_10 (not_10_out, number[4]);
  not not_11 (not_11_out, number[2]);
  not not_12 (not_12_out, number[0]);
  and and_1 (binary[2], not_1_out, not_2_out, not_3_out, not_4_out);
  and and_2 (binary[1], not_5_out, not_6_out, not_7_out, not_8_out);
  and and_3 (binary[0], not_9_out, not_10_out, not_11_out, not_12_out);
endmodule

module add1 (
  input  A,
  input  B,
  input  Cin,
  output Cout,
  output S
);

  wire and_1_out, and_2_out, xor_1_out;

  xor xor_1 (xor_1_out, A, B);
  and and_1 (and_1_out, A, B);
  and and_2 (and_2_out, xor_1_out, Cin);
  xor xor_2 (S, xor_1_out, Cin);
  or or_1 (Cout, and_1_out, and_2_out);
endmodule

module add2 (
  input  [1:0] B,
  input  [1:0] A,
  input  Cin,
  output Cout,
  output V,
  output [1:0] C
);

  wire add1_1_cout;

  add1 add1_1 (.A(A[0]), .B(B[0]), .Cin(Cin), .Cout(add1_1_cout), .S(C[0]));
  add1 add1_2 (.A(A[1]), .B(B[1]), .Cin(add1_1_cout), .Cout(Cout), .S(C[1]));
  xor xor_1 (V, Cout, add1_1_cout);
endmodule

module add4 (
  input  [3:0] B,
  input  [3:0] A,
  output Cout,
  output [3:0] C
);

  wire add2_1_cout;

  add2 add2_1 (.B(B[1:0]), .A(A[1:0]), .Cout(add2_1_cout), .C(C[1:0]));  // open: Cin, V
  add2 add2_2 (.B(B[3:2]), .A(A[3:2]), .Cin(add2_1_cout), .Cout(Cout), .C(C[3:2]));  // open: V
endmodule

module calculator (
  input  [7:0] A,
  input  [7:0] B
);

  wire add4_1_cout, ones_display_1_a, ones_display_1_b, ones_display_1_c, ones_display_1_d, ones_display_1_e,
       ones_display_1_f, ones_display_1_g, tenss_display_1_a, tenss_display_1_b, tenss_display_1_c,
       tenss_display_1_d, tenss_display_1_e, tenss_display_1_f, tenss_display_1_g;
  wire [2:0] number_encoder_1_binary, number_encoder_2_binary;
  wire [3:0] add4_1_c, bit_extender_1_out, bit_extender_2_out;

  number_encoder number_encoder_1 (.number(A), .binary(number_encoder_1_binary));
  number_encoder number_encoder_2 (.number(B), .binary(number_encoder_2_binary));
  assign bit_extender_1_out = {{1{1'b0}}, number_encoder_2_binary};  // Bit_Extender bit_extender_1
  assign bit_extender_2_out = {{1{1'b0}}, number_encoder_1_binary};  // Bit_Extender bit_extender_2
  add4 add4_1 (.B(bit_extender_2_out), .A(bit_extender_1_out), .Cout(add4_1_cout), .C(add4_1_c));
  tenss_display tenss_display_1 (
    .A_3(add4_1_c[3]), .A_2(add4_1_c[2]), .A_1(add4_1_c[1]), .A_0(add4_1_c[0]), .zero(add4_1_cout),
    .f(tenss_display_1_f), .a(tenss_display_1_a), .b(tenss_display_1_b), .g(tenss_display_1_g),
    .e(tenss_display_1_e), .d(tenss_display_1_d), .c(tenss_display_1_c));
  ones_display ones_display_1 (
    .A_3(add4_1_c[3]), .A_2(add4_1_c[2]), .A_1(add4_1_c[1]), .A_0(add4_1_c[0]), .f(ones_display_1_f),
    .a(ones_display_1_a), .b(ones_display_1_b), .g(ones_display_1_g), .e(ones_display_1_e),
    .d(ones_display_1_d), .c(ones_display_1_c));
  _7_Segment_Display u_7_segment_display_1 (
    .g(tenss_display_1_g), .f(tenss_display_1_f), .a(tenss_display_1_a), .b(tenss_display_1_b),
    .e(tenss_display_1_e), .d(tenss_display_1_d), .c(tenss_display_1_c));  // open: dp
  _7_Segment_Display u_7_segment_display_2 (
    .g(ones_display_1_g), .f(ones_display_1_f), .a(ones_display_1_a), .b(ones_display_1_b),
    .e(ones_display_1_e), .d(ones_display_1_d), .c(ones_display_1_c));  // open: dp
endmodule

module ones_display (
  input  A_3,
  input  A_2,
  input  A_1,
  input  A_0,
  output f,
  output a,
  output b,
  output g,
  output e,
  output d,
  output c
);

  wire and_1_out, and_2_out, and_3_out, and_4_out, and_5_out, and_6_out, and_7_out, and_8_out, and_9_out,
       and_10_out, and_11_out, and_12_out, and_13_out, and_14_out, and_15_out, and_16_out, and_17_out,
       and_18_out, and_19_out, and_20_out, and_21_out, and_22_out, and_23_out, and_24_out, and_25_out,
       and_26_out, and_27_out, and_28_out, and_29_out, and_30_out, not_1_out, not_2_out, not_3_out,
       not_4_out, not_5_out, not_6_out, not_7_out, not_8_out, not_9_out, not_10_out, not_11_out, not_12_out,
       not_13_out, not_14_out, not_15_out, not_16_out, not_17_out, not_18_out, not_19_out, not_20_out,
       not_21_out, not_22_out, not_23_out, not_24_out, not_25_out, not_26_out, not_27_out, not_28_out,
       not_29_out, not_30_out, not_31_out, not_32_out, not_33_out, not_34_out, not_35_out, not_36_out,
       not_37_out, not_38_out, not_39_out, not_40_out;

  not not_1 (not_1_out, A_3);
  not not_2 (not_2_out, A_1);
  and and_1 (and_1_out, not_1_out, not_2_out, not_3_out);
  not not_3 (not_3_out, A_0);
  not not_4 (not_4_out, A_3);
  and and_2 (and_2_out, not_4_out, A_2, not_5_out);
  not not_5 (not_5_out, A_1);
  not not_6 (not_6_out, A_3);
  and and_3 (and_3_out, not_6_out, A_2, not_7_out);
  not not_7 (not_7_out, A_0);
  not not_8 (not_8_out, A_2);
  and and_4 (and_4_out, A_3, not_8_out, not_9_out);
  not not_9 (not_9_out, A_1);
  not not_10 (not_10_out, A_2);
  and and_5 (and_5_out, A_3, not_10_out, not_11_out);
  not not_11 (not_11_out, A_0);
  and and_6 (and_6_out, A_3, A_2, A_1);
  not not_12 (not_12_out, A_2);
  and and_7 (and_7_out, not_12_out, not_13_out);
  not not_13 (not_13_out, A_0);
  not not_14 (not_14_out, A_3);
  and and_8 (and_8_out, not_14_out, A_1);
  and and_9 (and_9_out, A_2, A_0);
  and and_10 (and_10_out, A_3, not_15_out);
  not not_15 (not_15_out, A_1);
  not not_16 (not_16_out, A_2);
  not not_17 (not_17_out, A_1);
  and and_11 (and_11_out, not_17_out, not_18_out);
  not not_18 (not_18_out, A_0);
  and and_12 (and_12_out, A_1, A_0);
  not not_19 (not_19_out, A_3);
  not not_20 (not_20_out, A_2);
  and and_13 (and_13_out, not_19_out, not_20_out, A_1);
  and and_14 (and_14_out, A_2, not_21_out);
  not not_21 (not_21_out, A_1);
  and and_15 (and_15_out, A_2, not_22_out);
  not not_22 (not_22_out, A_0);
  and and_16 (and_16_out, A_3, not_23_out);
  not not_23 (not_23_out, A_1);
  and and_17 (and_17_out, A_3, A_2);
  not not_24 (not_24_out, A_2);
  and and_18 (and_18_out, not_24_out, not_25_out);
  not not_25 (not_25_out, A_0);
  not not_26 (not_26_out, A_3);
  and and_19 (and_19_out, not_26_out, A_1, not_27_out);
  not not_27 (not_27_out, A_0);
  not not_28 (not_28_out, A_1);
  and and_20 (and_20_out, A_3, not_28_out, not_29_out);
  not not_29 (not_29_out, A_0);
  and and_21 (and_21_out, A_3, A_2, A_1, A_0);
  not not_30 (not_30_out, A_2);
  and and_22 (and_22_out, not_30_out, not_31_out);
  not not_31 (not_31_out, A_0);
  not not_32 (not_32_out, A_3);
  and and_23 (and_23_out, not_32_out, not_33_out, A_1);
  not not_33 (not_33_out, A_2);
  not not_34 (not_34_out, A_3);
  and and_24 (and_24_out, not_34_out, A_1, not_35_out);
  not not_35 (not_35_out, A_0);
  not not_36 (not_36_out, A_1);
  and and_25 (and_25_out, A_2, not_36_out, A_0);
  and and_26 (and_26_out, A_3, not_37_out);
  not not_37 (not_37_out, A_1);
  and and_27 (and_27_out, A_3, A_2, A_0);
  not not_38 (not_38_out, A_3);
  and and_28 (and_28_out, not_38_out, not_39_out);
  not not_39 (not_39_out, A_1);
  and and_29 (and_29_out, A_2, A_1);
  and and_30 (and_30_out, A_3, not_40_out);
  not not_40 (not_40_out, A_2);
  or or_1 (a, and_7_out, and_8_out, and_9_out, and_10_out);
  or or_2 (b, not_16_out, and_11_out, and_12_out, A_3);
  or or_3 (g, and_13_out, and_14_out, and_15_out, and_16_out, and_17_out);
  or or_4 (e, and_18_out, and_19_out, and_20_out, and_21_out);
  or or_5 (c, and_28_out, A_0, and_29_out, and_30_out);
  or or_6 (f, and_1_out, and_2_out, and_3_out, and_4_out, and_5_out, and_6_out);
  or or_7 (d, and_22_out, and_23_out, and_24_out, and_25_out, and_26_out, and_27_out);
endmodule

module tenss_display (
  input  A_3,
  input  A_2,
  input  A_1,
  input  A_0,
  input  zero,
  output f,
  output a,
  output b,
  output g,
  output e,
  output d,
  output c
);

  wire and_1_out, and_2_out, and_3_out, and_4_out, and_5_out, not_1_out, not_2_out, not_3_out, not_4_out,
       not_5_out, not_6_out, not_8_out, not_9_out, not_10_out, not_11_out, not_12_out, not_13_out;

  not not_1 (not_1_out, A_3);
  not not_2 (not_2_out, A_2);
  and and_1 (and_1_out, not_2_out, not_3_out);
  not not_3 (not_3_out, A_1);
  and and_2 (and_2_out, A_2, A_1, A_0);
  not not_4 (not_4_out, A_3);
  not not_5 (not_5_out, A_2);
  and and_3 (and_3_out, not_5_out, not_6_out);
  not not_6 (not_6_out, A_1);
  not not_7 (b, zero);
  not not_8 (not_8_out, A_3);
  not not_9 (not_9_out, A_2);
  and and_4 (and_4_out, not_9_out, not_10_out);
  not not_10 (not_10_out, A_1);
  not not_11 (not_11_out, A_3);
  not not_12 (not_12_out, A_2);
  and and_5 (and_5_out, not_12_out, not_13_out);
  not not_13 (not_13_out, A_1);
  not not_14 (c, zero);
  or or_1 (f, not_1_out, and_1_out, and_2_out);
  or or_2 (a, not_4_out, and_3_out);
  or or_3 (e, not_8_out, and_4_out);
  or or_4 (d, not_11_out, and_5_out);

  assign g = zero;
endmodule

module add3 (
  input  [2:0] B,
  input  [2:0] A,
  output [3:0] C
);

  wire add2_1_cout;

  add2 add2_1 (.B(B[1:0]), .A(A[1:0]), .Cout(add2_1_cout), .C(C[1:0]));  // open: Cin, V
  add1 add1_1 (.A(B[2]), .B(A[2]), .Cin(add2_1_cout), .Cout(C[3]), .S(C[2]));
endmodule
